# Fritzing sketch universal_wx (saved by Fritzing 0.9.4)
circuit board: 8.41256cm x 4.48466cm

parts:
  SPEED = RJ11 Jack [package=rj11-6]
  RAIN = RJ11 Jack [package=rj11-6]
  DIREC = RJ11 Jack [package=rj11-6]
  U1 = atmega328 [package=dip]
  BME280 = female pin header, 4 pins [form="♀ (female)"]
  SL1145 = female pin header, 4 pins [form="♀ (female)"]
  DS18B20 = female pin header, 3 pins [form="♀ (female)"]
  R1 = Resistor [tolerance=±5% resistance=10k package=THT]
  R2 = Resistor [tolerance=±5% resistance=10k package=THT]
  PWR = Power plug
  LED1 = LED - 5mm [color="Green (570nm)" package="5 mm [THT]"]
  LED2 = LED - 5mm [color="Red (633nm)" package="5 mm [THT]"]
  R3 = Resistor [tolerance=±5% resistance=100 package=THT]
  RST = Pushbutton [package=THT]
  R4 = Resistor [tolerance=±5% resistance=220 package=THT]
  R5 = Resistor [tolerance=±5% resistance=680 package=THT]
  SIM800L = female pin header, 6 pins [form="♀ (female)"]
  U2 = Voltage Regulator - 3.3V [package="TO220 [THT]"]
  U3 = Voltage Regulator [package=to220-adj]
  R6 = Resistor [tolerance=±5% resistance=150 package=THT]
  R7 = Resistor [tolerance=±5% resistance=330 package=THT]
  ANT1 = Antenna
  R8 = Resistor [tolerance=±5% resistance=10k package=THT]
  PRG = male pin header, 2 pins [form="♂ (male)"]
  R9 = Resistor [tolerance=±5% resistance=4.7k package="2512 [SMD]"]

nets:
  N1: SPEED.3, U1.D2, R1.Pin_1
  GND: SPEED.4, RAIN.4, DIREC.2, DIREC.4, U1.GND, BME280.pin2, SL1145.pin2, DS18B20.pin3, PWR.GND, LED1.cathode, LED2.cathode, RST.leg0, SIM800L.pin6, U2.GND, R7.Pin_1
  N2: RAIN.3, DIREC.3, U1.D3_(PWM), R2.Pin_1
  N3: DIREC.5, U1.A0, R8.Pin_1
  N4: U1.RESET, RST.leg1, R4.Pin_1
  N5: U1.D0_(RX), PRG.pin2
  N6: U1.D1_(TX), PRG.pin1
  N7: U1.VCC, U1.AVCC, U1.AREF, BME280.pin1, SL1145.pin1, DS18B20.pin1, R1.Pin_0, R2.Pin_0, R4.Pin_0, U2.output_voltage, R8.Pin_0, R9.Pin_0
  N8: U1.D9_(PWM), SIM800L.pin3
  N9: U1.D10_(PWM), SIM800L.pin5
  N10: U1.D11_(PWM), SIM800L.pin4
  N11: U1.D12, DS18B20.pin2, R9.Pin_1
  N12: U1.D13, R3.Pin_0
  N13: U1.A4, BME280.pin4, SL1145.pin4
  N14: U1.A5, BME280.pin3, SL1145.pin3
  N15: PWR.VCC, R5.Pin_0, U2.input_voltage, U3.IN
  N16: LED1.anode, R5.Pin_1
  N17: LED2.anode, R3.Pin_1
  N18: SIM800L.pin1, ANT1.antenna_lead
  N19: SIM800L.pin2, U3.OUT, R6.Pin_1
  N20: U3.ADJ, R6.Pin_0, R7.Pin_0

notes:
  WX
  Wind Speed
  Rainfall
  Wind Direction/Speed
  Temp/Hum/Pressure
  UV/IR/Visible
  Soil Temp
  GSM/GPRS Module
  Logic Voltage Regulator
  GSM Module Voltage Regulator
  Status
  Power
  6~15V
